# Fritzing sketch arduino-nano-motor-controller (saved by Fritzing 1.0.1rc)
circuit board: 4.01832cm x 3.65172cm
breadboards: 1

parts:
  P+_P-_D+_D-_E+_E-_A+_A- = female pin header, 8 pins [form="♀ (female)"]
  Nano1 = Arduino Nano v2.3
  Vin = female pin header, 2 pins [form="♀ (female)"]
  5v = female pin header, 2 pins [form="♀ (female)"]
  L1 = female pin header, 2 pins [form="♀ (female)"]
  L2 = female pin header, 2 pins [form="♀ (female)"]

nets:
  GND: P+_P-_D+_D-_E+_E-_A+_A-.pin1, P+_P-_D+_D-_E+_E-_A+_A-.pin3, P+_P-_D+_D-_E+_E-_A+_A-.pin5, P+_P-_D+_D-_E+_E-_A+_A-.pin7, Nano1.GND, Vin.pin2, 5v.pin1, L1.pin2, L2.pin2
  ALM: P+_P-_D+_D-_E+_E-_A+_A-.pin2, Nano1.D2
  ENA: P+_P-_D+_D-_E+_E-_A+_A-.pin4, Nano1.D7
  DIR: P+_P-_D+_D-_E+_E-_A+_A-.pin6, Nano1.D8
  PUL: P+_P-_D+_D-_E+_E-_A+_A-.pin8, Nano1.D9
  LIMIT: Nano1.D5, L1.pin1
  N1: Nano1.D10, L2.pin1
  LED: Nano1.D13
  N2: Nano1.+5V, 5v.pin2
  N3: Nano1.VIN, Vin.pin1

notes:
  the moment before
  van der Maesen de Sombreff
  Mauricio
  2025
